# Fritzing sketch MH-Z16_I2C_Schematic (saved by Fritzing 0.9.7b)

parts:
  Grove1 = Grove 3 Axis Digital Accelerometer 16g
  Part4 = Arduino Ethernet Shield (Rev3)

nets:
  GND: Grove1.GND, Part4.GND
  VCC: Grove1.VCC, Part4.5V
  N1: Grove1.SDA, Part4.A4/SDA
  N2: Grove1.SCL, Part4.A5/SCL
